# Fritzing sketch Circuit (saved by Fritzing 0.9.3b)
breadboards: 1

parts:
  R1 = Photocell (LDR) [package=THT]
  J1 = STM32 Nucleo boards
  R2 = Resistor [tolerance=±5% resistance=220 package=THT]
  R3 = Temperature Sensor (Thermistor) [thermistor_type=NTC package=THT]
  R4 = Resistor [tolerance=±5% resistance=220 package=THT]
  J2 = Piezo Speaker
  Componente1 = Solid State High Level Relay Module [package=relay]
  Componente2 = Solid State High Level Relay Module [package=relay]
  R5 = 220 Ω Resistor [package=THT]  # not connected
  M1 = DC Motor  # not connected
  Lightbulb_socket1 = Bulb holder (E10) with base  # not connected

nets:
  N1: R1.pin_0, J1.A0, R2.Pin_1
  N2: R1.pin_1, J1.5V, R3.pin_0, Componente1.DC+, Componente2.DC+
  N3: J1.A1, R3.pin_1, R4.Pin_1
  N4: J1.D2, J2.pin2
  N5: J1.D4, Componente1.CH1
  N6: J1.D7, Componente2.CH1
  N7: J1.GND, R2.Pin_0, R4.Pin_0, J2.pin1, Componente2.DC-

custom parts:
  Solid State High Level Relay Module: 5V Omron solid state relay 240V 2A output with resistance fuse.
  220 Ω Resistor: A generic resistor (0.25W)
  Bulb holder (E10) with base: A bulb holder for an E10 bulb with a base.
